# Fritzing sketch WiFi_Device_Sketch (saved by Fritzing 1.0.1rc)

parts:
  M1 = Humidity and Temperature Sensor DHT11
  DHT1 = DHT22 Humidity and Temperature Sensor
  DS1 = DS18B20 1-Wire Temperature Sensor Probe
  J1 = Basic Servo
  IC1 = DIP - 6 pins [chip_label="5V RELAY" package="DIP (Dual Inline) [THT]"]
  IC4 = DIP - 6 pins [chip_label="5V RELAY" package="DIP (Dual Inline) [THT]"]
  IC3 = DIP - 6 pins [chip_label="5V RELAY" package="DIP (Dual Inline) [THT]"]
  IC2 = DIP - 6 pins [chip_label="5V RELAY" package="DIP (Dual Inline) [THT]"]
  R2 = Resistor [tolerance=±5% resistance=10k package="2010 [SMD]"]
  R3 = Resistor [tolerance=±5% resistance=10k package="2010 [SMD]"]
  U1 = TXS0108 [part_number=TXS0108EPW package=TSSOP]
  U2 = TXS0108 [part_number=TXS0108EPW package=TSSOP]
  U3 = TXS0108 [part_number=TXS0108EPW package=TSSOP]
  VCC1 = 4 x AAA Battery Mount
  C1 = Capacitor [package=1210]
  C2 = Capacitor [package=1206]
  C3 = Capacitor [package=1210]
  C4 = Capacitor [package=1210]
  Z1 = VARISTOR [package=0603-res]
  Z2 = VARISTOR [package=0603-res]
  Z3 = VARISTOR [package=0603-res]
  C5 = Capacitor [package=1210]
  C6 = Capacitor [package=1210]
  J2 = Camdenboss CTB0158-4 [part_number=CTB0158-4 package=THT]
  J3 = Camdenboss CTB0158-5 [part_number=CTB0158-5 package=THT]
  J4 = Camdenboss CTB0158-2 [part_number=CTB0158-2 package=THT]

nets:
  VDD: M1.Vcc, DHT1.VDD, DS1.VDD, R3.Pin_0
  N1: M1.Data, R2.Pin_1, U1.B4
  GND: M1.GND, DHT1.GND, DS1.GND
  N2: DHT1.DATA, R3.Pin_1, U1.B5
  N3: DS1.DQ, U1.B6
  GND_2: J1.gnd, IC1.DC-, IC4.DC-, IC3.DC-, IC2.DC-, U2.GND, U3.GND, VCC1.-, C1.2, C2.2, C3.2, C4.2, Z1.1, Z2.1
  N4: J1.vcc, U2.VccB, U3.VccB, VCC1.+, C1.1, C4.1
  N5: J1.pulse, U2.B4
  N6: IC1.IN, U3.B7
  N7: IC4.DC+, IC3.DC+, IC2.DC+
  N8: IC4.IN, U3.B4
  N9: IC3.IN, U3.B5
  N10: IC2.IN, U3.B6
  N11: U1.VccA, U2.VccA, U3.VccA, C2.1, C3.1, C6.2
  N12: U1.A4, J2.pin4
  N13: U1.A5, J2.pin3
  N14: U1.A6, J2.pin2
  N15: U1.OE, Z3.2, J2.pin1
  N16: U1.GND, Z3.1, C5.1, C6.1
  N17: U1.VccB, C5.2
  N18: U2.A4, J4.pin2
  N19: U2.OE, Z2.2, J4.pin1
  N20: U3.A4, J3.pin5
  N21: U3.A5, J3.pin4
  N22: U3.A6, J3.pin3
  N23: U3.A7, J3.pin2
  N24: U3.OE, Z1.2, J3.pin1

custom parts:
  Humidity and Temperature Sensor DHT11: Digital relative humidity & temperature sensor DHT11
  DIP - 6 pins: A DIP stand-in part for whatever IC you want. With 6 pins on a 300mil dual inline package (DIP) footprint.
  TXS0108: This 8-bit non-inverting translator uses two separate configurable power-supply rails. The A port tracks the VCCA pin supply voltage. The VCCA pin accepts any supply voltage between 1.2 V and 3.6 V. The B port tracks the VCCB pin supply voltage. The VCCB pin accepts any supply voltage between 1.65 V and 5.5 V. Two input supply pins allows for low Voltage bidirectional translation between any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
